// Logisim project control_unit.circ as structural Verilog: 1 circuit, main circuit main
module main (
  input  [31:0] Instruction,
  output IsImmediate,
  output IsRegister,
  output IsTableB,
  output IsJump,
  output IsBranch,
  output IsMem,
  output [15:0] Immediate,
  output [15:0] Offset,
  output [25:0] JumpTarget,
  output [4:0] ShiftAmount,
  output [3:0] ALUOpCode,
  output ImmediateSelect,
  output ImmSignExt,
  output CompSign,
  output [4:0] Ra,
  output [4:0] Rb,
  output [4:0] Rd,
  output [1:0] PCSelect,
  output [2:0] BranchSelect,
  output MemLoad,
  output MemStore,
  output MemWord,
  output MemSignExt,
  output FuncField,
  output [1:0] SaControl,
  output [1:0] ASelect,
  output [1:0] ExecOut
);

  // Control control_1: pin names not known; wires that end beside it: IsImmediate, IsRegister, IsTableB, IsJump, IsBranch, IsMem, Immediate, Offset, JumpTarget, ShiftAmount
endmodule
